# Fritzing sketch Connection (saved by Fritzing 0.9.6b)
breadboards: 1

parts:
  WeMos_D1_Mini1 = WeMos D1 Mini
  Q1 = Basic FET P-Channel [part_number=L7805ABV package="TO220 [THT]"]
  R7 = Resistor [tolerance=±5% power=0.25 resistance=4.7k package=THT]
  C10 = Ceramic Capacitor [capacitance=0.47mF voltage=35V package="100 mil [THT, multilayer]"]
  C12 = Ceramic Capacitor [capacitance=0.47mF voltage=35V package="100 mil [THT, multilayer]"]

nets:
  N1: WeMos_D1_Mini1.RX, R7.Pin_0
  N2: Q1.gate, Q1.drain, C10.0, C10.1, C12.0
  N3: Q1.source, R7.Pin_1
